// Logisim project project_2_14_6.circ as structural Verilog
module DFlipFlop (
  input  D,
  input  Rst,
  output Q,
  output NotQ
);

  wire and_1_out, Clk_out, dlatch_1_q, not_1_out, not_2_out, not_3_out;

  Clock #(.highDuration(2), .lowDuration(2)) Clk (.out(Clk_out));
  Clock sysclk ();  // open: out
  not not_1 (not_1_out, Rst);
  not not_2 (not_2_out, Clk_out);
  and and_1 (and_1_out, D, not_1_out);
  not not_3 (not_3_out, not_2_out);
  DLatch dlatch_1 (.D(and_1_out), .Clk(not_2_out), .Q(dlatch_1_q));  // open: NotQ
  DLatch dlatch_2 (.D(dlatch_1_q), .Clk(not_3_out), .Q(Q), .NotQ(NotQ));
endmodule

module DLatch (
  input  D,
  input  Clk,
  output Q,
  output NotQ
);

  wire nand_1_out, nand_2_out, not_1_out;

  Clock sysclk ();  // open: out
  not not_1 (not_1_out, D);
  nand nand_1 (nand_1_out, D, Clk);
  nand nand_2 (nand_2_out, Clk, not_1_out);
  nand nand_3 (Q, nand_1_out, NotQ);
  nand nand_4 (NotQ, Q, nand_2_out);
endmodule

module JKFlipFlop (
  input  Init,
  input  J,
  input  K,
  input  Rst,
  output Q,
  output NotQ
);

  wire and_1_out, and_2_out, and_3_out, Clk_out, not_1_out, not_2_out, or_1_out, or_2_out, or_3_out,
       srlatch_1_notq, srlatch_1_q;

  Clock #(.highDuration(2), .lowDuration(2)) Clk (.out(Clk_out));
  Clock sysclk ();  // open: out
  not not_1 (not_1_out, Rst);
  and and_1 (and_1_out, J, not_1_out);
  or or_1 (or_1_out, K, Rst);
  and and_2 (and_2_out, NotQ, and_1_out);
  and and_3 (and_3_out, or_1_out, Q);
  or or_2 (or_2_out, Rst, Clk_out);
  not not_2 (not_2_out, Clk_out);
  SRLatch srlatch_1 (.S(and_2_out), .Clk(or_2_out), .R(and_3_out), .Q(srlatch_1_q), .NotQ(srlatch_1_notq));
  or or_3 (or_3_out, Rst, not_2_out);
  SRLatch srlatch_2 (.S(srlatch_1_q), .Clk(or_3_out), .R(srlatch_1_notq), .Q(Q), .NotQ(NotQ));
endmodule

module SRLatch (
  input  S,
  input  Clk,
  input  R,
  output Q,
  output NotQ
);

  wire nand_1_out, nand_2_out;

  Clock sysclk ();  // open: out
  nand nand_1 (nand_1_out, S, Clk);
  nand nand_2 (nand_2_out, Clk, R);
  nand nand_3 (Q, nand_1_out, NotQ);
  nand nand_4 (NotQ, Q, nand_2_out);
endmodule
